// Logisim project PC.circ as structural Verilog: 14 circuits, main circuit main
module main (
  input  RESET,
  output [15:0] out_2,
  output [15:0] out_3
);

  wire and_1_out, and_2_out, button_1_out, button_2_out, button_3_out, button_4_out, button_5_out, CLOCK_out,
       ic_1_int, ic_1_intr, keyboard_1_int, mc_1_er0, mc_1_er1, mc_1_er2, mc_1_erk, mc_1_ew0, mc_1_ew1,
       mc_1_ew2, not_1_out, processor_1_inta, processor_1_mem_r, processor_1_out_9, processor_1_out_10,
       processor_1_readint;
  wire [15:0] led_1_out_6, led_1_out_7, led_1_out_8, led_1_out_9, led_1_out_10, led_1_out_11, led_1_out_12,
       led_1_out_13, led_1_out_14, led_1_out_15, led_1_out_16, led_1_out_17, led_1_out_18, led_1_out_19,
       led_1_out_20, led_1_out_21;

  and and_1 (and_1_out, not_1_out, CLOCK_out);
  Button button_1 (.out(button_1_out));
  Counter #(.width(32), .max('hffffffff)) counter_1 (.clk(and_1_out), .clr(RESET));  // open: load, D, count, Q, carry
  Clock CLOCK (.out(CLOCK_out));
  IC ic_1 (
    ._0(button_1_out), ._1(keyboard_1_int), ._2(1'b0), ._3(1'b0), .INTR(ic_1_intr), .CLK(CLOCK_out),
    .DATA(out_3), .INT(ic_1_int), .INTA(processor_1_inta), .R(mc_1_er1), .W(mc_1_ew1), .Reset(RESET));
  and and_2 (and_2_out, CLOCK_out, not_1_out);
  Processor processor_1 (
    .Clock(and_2_out), .Reset(RESET), .Address(out_2), .Data_Out(out_3), .Data_In(out_3),
    .Mem_R(processor_1_mem_r), .out_9(processor_1_out_9), .out_10(processor_1_out_10), .INT(ic_1_int),
    .INTR(ic_1_intr), .INTA(processor_1_inta), .ReadInt(processor_1_readint));
  not not_1 (not_1_out, processor_1_out_10);
  MC mc_1 (
    .ADRESS(out_2), .EW(processor_1_out_9), .ER(processor_1_mem_r), .ReadInt(processor_1_readint),
    .EW0(mc_1_ew0), .ER0(mc_1_er0), .EW1(mc_1_ew1), .ER1(mc_1_er1), .EW2(mc_1_ew2), .ER2(mc_1_er2),
    .ERK(mc_1_erk));  // open: EWK
  Hex_Digit_Display hex_digit_display_1 (.value(out_2[11:8]));  // open: dp
  Hex_Digit_Display hex_digit_display_2 (.value(out_2[15:12]));  // open: dp
  Hex_Digit_Display hex_digit_display_3 (.value(out_2[7:4]));  // open: dp
  Hex_Digit_Display hex_digit_display_4 (.value(out_2[3:0]));  // open: dp
  LED led_1 (
    .CLOCK(CLOCK_out), .RESET(RESET), .DATA(out_3), .EW(mc_1_ew2), .ADDRES(out_2[3:0]), .out_6(led_1_out_6),
    .out_7(led_1_out_7), .out_8(led_1_out_8), .out_9(led_1_out_9), .out_10(led_1_out_10),
    .out_11(led_1_out_11), .out_12(led_1_out_12), .out_13(led_1_out_13), .out_14(led_1_out_14),
    .out_15(led_1_out_15), .out_16(led_1_out_16), .out_17(led_1_out_17), .out_18(led_1_out_18),
    .out_19(led_1_out_19), .out_20(led_1_out_20), .out_21(led_1_out_21));
  DotMatrix #(.inputtype("row"), .matrixcols(16), .matrixrows(16)) dotmatrix_1 (
    .row0(led_1_out_6), .row1(led_1_out_7), .row2(led_1_out_8), .row3(led_1_out_9), .row4(led_1_out_10),
    .row5(led_1_out_11), .row6(led_1_out_12), .row7(led_1_out_13), .row8(led_1_out_14), .row9(led_1_out_15),
    .row10(led_1_out_16), .row11(led_1_out_17), .row12(led_1_out_18), .row13(led_1_out_19),
    .row14(led_1_out_20), .row15(led_1_out_21));
  Memory memory_1 (.Address(out_2), .CLOCK(CLOCK_out), .W(mc_1_ew0), .R(mc_1_er0), .Data_In(out_3), .Data_Out(out_3));
  // Memory memory_2: pin names not known; wires that end beside it: out_2, out_3, out_3, mc_1_ew2, mc_1_er2, CLOCK_out
  Button button_2 (.out(button_2_out));
  Button button_3 (.out(button_3_out));
  Button button_4 (.out(button_4_out));
  Button button_5 (.out(button_5_out));
  Keyboard keyboard_1 (
    .Clock(CLOCK_out), .Res(RESET), .Data(out_3), .INT(keyboard_1_int), .ER(mc_1_erk), .in_1(button_2_out),
    .in_2(button_3_out), .in_3(button_4_out), .in_4(button_5_out));
endmodule

module Processor (
  input  Clock,
  input  Reset,
  input  [15:0] Data_In,
  input  INT,
  input  INTR,
  output [15:0] Address,
  output [15:0] Data_Out,
  output Mem_R,
  output out_9,
  output out_10,
  output ReadInt,
  output INTA
);

  wire ALU_OUT_E, control_unit_1_mfc, control_unit_1_mfd, D1, D2, DATA, EW, FLAGS_W, IP, MUX_A, MUX_DATA,
       MUX_OP2, OP_r1, OP_r2;
  wire [1:0] MUX_Address, MUX_AW, MUX_B, MUX_DW;
  wire [3:0] control_unit_1_alu_op, multiplexer_3_out;
  wire [15:0] A_IP, alu_1_flags_c, alu_1_flags_d, ALU_OUT, bit_extender_1_out, control_unit_1_fc,
       control_unit_1_fd, controlled_buffer_2_out, controlled_buffer_3_out, Data_Out_t, FLAGS_C, FLAGS_D,
       FLAGS_OUT, multiplexer_1_out, multiplexer_2_out, multiplexer_4_out, multiplexer_5_out,
       multiplexer_6_out, OP_1, OP_2, register_3_q, register_4_a, register_4_b, register_5_q, register_7_q;

  assign Data_Out = out_9 ? multiplexer_1_out : 16'bz;  // Controlled_Buffer controlled_buffer_1
  assign controlled_buffer_2_out = Mem_R ? Data_In : 16'bz;  // Controlled_Buffer controlled_buffer_2
  Multiplexer #(.width(16)) multiplexer_1 (
    .in0(Data_Out_t), .in1(OP_2), .out(multiplexer_1_out), .sel(MUX_DATA), .en(1'b1));
  Register_part #(.width(16)) register_1 (.D(controlled_buffer_2_out), .en(OP_r1), .Q(OP_1), .clk(Clock), .clr(Reset));
  Register_part #(.width(16)) register_2 (.D(controlled_buffer_2_out), .en(OP_r2), .Q(OP_2), .clk(Clock), .clr(Reset));
  Register_part #(.width(16)) register_3 (
    .D(controlled_buffer_2_out), .en(DATA), .Q(register_3_q), .clk(Clock), .clr(Reset));
  assign bit_extender_1_out = {{12{1'b0}}, OP_1[15:12]};  // Bit_Extender bit_extender_1
  Multiplexer #(.width(16)) multiplexer_2 (
    .in0(OP_2), .in1(bit_extender_1_out), .out(multiplexer_2_out), .sel(MUX_OP2), .en(1'b1));
  Control_Unit control_unit_1 (
    .OP_1(OP_1), .OP_2(OP_2), .OP_r1(OP_r1), .OP_r2(OP_r2), .DATA(DATA), .EW(EW), .D1(D1), .D2(D2),
    .MUX_DW(MUX_DW), .MUX_A(MUX_A), .MUX_B(MUX_B), .MUX_Address(MUX_Address), .Mem_R(Mem_R), .IP(IP),
    .ALU_OP(control_unit_1_alu_op), .CLOCK(Clock), .RES(Reset), .Mem_W(out_9), .FLAGS_W(FLAGS_W),
    .MUX_AW(MUX_AW), .MUX_DATA(MUX_DATA), .ALU_OUT(ALU_OUT_E), .FLAGS(FLAGS_OUT), .MUX_OP2(MUX_OP2),
    .out_30(out_10), .INT(INT), .INTR(INTR), .INTA(INTA), .ReadInt(ReadInt), .FC(control_unit_1_fc),
    .FD(control_unit_1_fd), .MFD(control_unit_1_mfd), .MFC(control_unit_1_mfc));
  Hex_Digit_Display hex_digit_display_1 (.value(OP_1[15:12]));  // open: dp
  Hex_Digit_Display hex_digit_display_2 (.value(OP_1[11:8]));  // open: dp
  Hex_Digit_Display hex_digit_display_3 (.value(OP_1[7:4]));  // open: dp
  Multiplexer #(.select(2), .width(4)) multiplexer_3 (
    .in0(OP_1[15:12]), .in1(OP_1[11:8]), .in2(OP_1[7:4]), .in3(4'b1101), .out(multiplexer_3_out),
    .sel(MUX_AW), .en(1'b1));
  Multiplexer #(.select(2), .width(16)) multiplexer_4 (
    .in0(register_3_q), .in1(ALU_OUT), .in2(A_IP), .in3(multiplexer_2_out), .out(multiplexer_4_out),
    .sel(MUX_DW), .en(1'b1));
  Hex_Digit_Display hex_digit_display_4 (.value(OP_1[3:0]));  // open: dp
  Register register_4 (
    .A1(OP_1[7:4]), .in_4(EW), .A3(multiplexer_3_out), .DW(multiplexer_4_out), .A2(OP_1[11:8]),
    .A(register_4_a), .B(register_4_b), .in_1(Clock), .in_2(Reset), .FLAGS(FLAGS_OUT), .Data_Flags(FLAGS_D),
    .Control_Flags(controlled_buffer_3_out), .out_12(A_IP));
  Hex_Digit_Display hex_digit_display_5 (.value(OP_2[11:8]));  // open: dp
  Hex_Digit_Display hex_digit_display_6 (.value(OP_2[15:12]));  // open: dp
  assign controlled_buffer_3_out = FLAGS_W ? FLAGS_C : 16'bz;  // Controlled_Buffer controlled_buffer_3
  Pull_Resistor pull_resistor_1 (.node(controlled_buffer_3_out));
  Hex_Digit_Display hex_digit_display_7 (.value(OP_2[3:0]));  // open: dp
  Hex_Digit_Display hex_digit_display_8 (.value(OP_2[7:4]));  // open: dp
  Register_part #(.width(16)) register_5 (.D(register_4_a), .en(D1), .Q(register_5_q), .clk(Clock), .clr(Reset));
  Register_part #(.width(16)) register_6 (.D(register_4_b), .en(D2), .Q(Data_Out_t), .clk(Clock), .clr(Reset));
  Multiplexer #(.width(16)) multiplexer_5 (
    .in0(A_IP), .in1(register_5_q), .out(multiplexer_5_out), .sel(MUX_A), .en(1'b1));
  Multiplexer #(.select(2), .width(16)) multiplexer_6 (
    .in0(Data_Out_t), .in1(16'h1), .in2(multiplexer_2_out), .in3({16{1'b0}}), .out(multiplexer_6_out),
    .sel(MUX_B), .en(1'b1));
  ALU alu_1 (
    .A(multiplexer_5_out), .B(multiplexer_6_out), .ALU_OP(control_unit_1_alu_op), .out_5(ALU_OUT),
    .FLAGS_D(alu_1_flags_d), .Ci(FLAGS_OUT[0]), .FLAGS_C(alu_1_flags_c));
  Multiplexer #(.width(16)) multiplexer_7 (
    .in0(alu_1_flags_d), .in1(control_unit_1_fd), .out(FLAGS_D), .sel(control_unit_1_mfd), .en(1'b1));
  Register_part #(.width(16)) register_7 (.D(ALU_OUT), .en(ALU_OUT_E), .Q(register_7_q), .clk(Clock), .clr(Reset));
  Multiplexer #(.width(16)) multiplexer_8 (
    .in0(alu_1_flags_c), .in1(control_unit_1_fc), .out(FLAGS_C), .sel(control_unit_1_mfc), .en(1'b1));
  Hex_Digit_Display hex_digit_display_9 (.value(A_IP[15:12]));  // open: dp
  Hex_Digit_Display hex_digit_display_10 (.value(A_IP[11:8]));  // open: dp
  Hex_Digit_Display hex_digit_display_11 (.value(A_IP[3:0]));  // open: dp
  Hex_Digit_Display hex_digit_display_12 (.value(A_IP[7:4]));  // open: dp
  Multiplexer #(.select(2), .width(16)) multiplexer_9 (
    .in0(A_IP), .in1(ALU_OUT), .in2(register_5_q), .in3(register_7_q), .out(Address), .sel(MUX_Address),
    .en(1'b1));
  ALU alu_2 ();  // open: A, B, ALU_OP, out_5, FLAGS_D, Ci, FLAGS_C

  // Other names for the same wires on the sheet: CLK = Clock; Mem_W = out_9; Res = Reset
endmodule

module Memory (
  input  [15:0] Address,
  input  CLOCK,
  input  W,
  input  R,
  input  [15:0] Data_In,
  output [15:0] Data_Out
);

  wire [7:0] ram_1_data, ram_2_data;
  wire [15:0] controlled_buffer_2_out, ram_3_data, undriven;

  RAM #(.addrWidth(16)) ram_1 (.addr(undriven), .data(ram_1_data), .sel(W), .clk(CLOCK), .ld(R), .clr(1'b0));
  RAM #(.addrWidth(16)) ram_2 (.addr(undriven), .data(ram_2_data), .sel(W), .clk(CLOCK), .ld(R), .clr(1'b0));
  RAM #(.addrWidth(16), .dataWidth(16), .bus("separate")) ram_3 (
    .addr(Address), .din(controlled_buffer_2_out), .data(ram_3_data), .str(W), .clk(CLOCK), .ld(R), .clr(1'b0));  // open: sel
  assign Data_Out = R ? ram_3_data : 16'bz;  // Controlled_Buffer controlled_buffer_1
  assign controlled_buffer_2_out = W ? Data_In : 16'bz;  // Controlled_Buffer controlled_buffer_2
endmodule

module Register (
  input  in_1,
  input  in_2,
  input  [3:0] A1,
  input  in_4,
  input  [3:0] A3,
  input  [15:0] DW,
  input  [15:0] Data_Flags,
  input  [15:0] Control_Flags,
  input  [3:0] A2,
  output [15:0] A,
  output [15:0] B,
  output [15:0] out_12,
  output [15:0] FLAGS
);

  wire decoder_2_out0, decoder_2_out1, decoder_2_out2, decoder_2_out3, decoder_2_out4, decoder_2_out5,
       decoder_2_out6, decoder_2_out7, decoder_2_out8, decoder_2_out9, decoder_2_out10, decoder_2_out11,
       decoder_2_out12, decoder_2_out13, decoder_2_out14, decoder_2_out15, decoder_3_out0, decoder_3_out1,
       decoder_3_out2, decoder_3_out3, decoder_3_out4, decoder_3_out5, decoder_3_out6, decoder_3_out7,
       decoder_3_out8, decoder_3_out9, decoder_3_out10, decoder_3_out11, decoder_3_out12, decoder_3_out13,
       decoder_3_out14, decoder_3_out15, pull_resistor_1_node, pull_resistor_2_node, pull_resistor_3_node,
       pull_resistor_4_node, pull_resistor_5_node, pull_resistor_6_node, pull_resistor_7_node,
       pull_resistor_8_node, pull_resistor_9_node, pull_resistor_10_node, pull_resistor_11_node,
       pull_resistor_12_node, pull_resistor_13_node, pull_resistor_14_node, pull_resistor_15_node,
       pull_resistor_16_node;
  wire [15:0] reg_sp_1_out_5, register_1_q, register_2_q, register_3_q, register_4_q, register_5_q,
       register_6_q, register_7_q, register_8_q, register_9_q, register_10_q, register_11_q, register_12_q,
       register_13_q;

  Pull_Resistor pull_resistor_1 (.node(pull_resistor_1_node));
  Pull_Resistor pull_resistor_2 (.node(pull_resistor_2_node));
  Pull_Resistor pull_resistor_3 (.node(pull_resistor_3_node));
  Pull_Resistor pull_resistor_4 (.node(pull_resistor_4_node));
  Pull_Resistor pull_resistor_5 (.node(pull_resistor_5_node));
  Pull_Resistor pull_resistor_6 (.node(pull_resistor_6_node));
  Pull_Resistor pull_resistor_7 (.node(pull_resistor_7_node));
  Pull_Resistor pull_resistor_8 (.node(pull_resistor_8_node));
  Pull_Resistor pull_resistor_9 (.node(pull_resistor_9_node));
  Pull_Resistor pull_resistor_10 (.node(pull_resistor_10_node));
  Pull_Resistor pull_resistor_11 (.node(pull_resistor_11_node));
  Pull_Resistor pull_resistor_12 (.node(pull_resistor_12_node));
  Pull_Resistor pull_resistor_13 (.node(pull_resistor_13_node));
  Pull_Resistor pull_resistor_14 (.node(pull_resistor_14_node));
  Pull_Resistor pull_resistor_15 (.node(pull_resistor_15_node));
  Pull_Resistor pull_resistor_16 (.node(pull_resistor_16_node));
  Decoder #(.select(4)) decoder_1 (
    .out0(pull_resistor_1_node), .out1(pull_resistor_2_node), .out2(pull_resistor_3_node),
    .out3(pull_resistor_4_node), .out4(pull_resistor_5_node), .out5(pull_resistor_6_node),
    .out6(pull_resistor_7_node), .out7(pull_resistor_8_node), .out8(pull_resistor_9_node),
    .out9(pull_resistor_10_node), .out10(pull_resistor_11_node), .out11(pull_resistor_12_node),
    .out12(pull_resistor_13_node), .out13(pull_resistor_14_node), .out14(pull_resistor_15_node),
    .out15(pull_resistor_16_node), .sel(A3), .en(in_4));
  Decoder #(.select(4)) decoder_2 (
    .out0(decoder_2_out0), .out1(decoder_2_out1), .out2(decoder_2_out2), .out3(decoder_2_out3),
    .out4(decoder_2_out4), .out5(decoder_2_out5), .out6(decoder_2_out6), .out7(decoder_2_out7),
    .out8(decoder_2_out8), .out9(decoder_2_out9), .out10(decoder_2_out10), .out11(decoder_2_out11),
    .out12(decoder_2_out12), .out13(decoder_2_out13), .out14(decoder_2_out14), .out15(decoder_2_out15),
    .sel(A2), .en(1'b1));
  Decoder #(.select(4)) decoder_3 (
    .out0(decoder_3_out0), .out1(decoder_3_out1), .out2(decoder_3_out2), .out3(decoder_3_out3),
    .out4(decoder_3_out4), .out5(decoder_3_out5), .out6(decoder_3_out6), .out7(decoder_3_out7),
    .out8(decoder_3_out8), .out9(decoder_3_out9), .out10(decoder_3_out10), .out11(decoder_3_out11),
    .out12(decoder_3_out12), .out13(decoder_3_out13), .out14(decoder_3_out14), .out15(decoder_3_out15),
    .sel(A1), .en(1'b1));
  Register_part #(.width(16)) register_1 (.en(pull_resistor_1_node), .Q(register_1_q), .clr(in_2));  // open: D, clk
  Register_part #(.width(16)) register_2 (.D(DW), .en(pull_resistor_2_node), .Q(register_2_q), .clk(in_1), .clr(in_2));
  Register_part #(.width(16)) register_3 (.D(DW), .en(pull_resistor_3_node), .Q(register_3_q), .clk(in_1), .clr(in_2));
  Register_part #(.width(16)) register_4 (.D(DW), .en(pull_resistor_4_node), .Q(register_4_q), .clk(in_1), .clr(in_2));
  Register_part #(.width(16)) register_5 (.D(DW), .en(pull_resistor_5_node), .Q(register_5_q), .clk(in_1), .clr(in_2));
  Register_part #(.width(16)) register_6 (.D(DW), .en(pull_resistor_6_node), .Q(register_6_q), .clk(in_1), .clr(in_2));
  Register_part #(.width(16)) register_7 (.D(DW), .en(pull_resistor_7_node), .Q(register_7_q), .clk(in_1), .clr(in_2));
  Register_part #(.width(16)) register_8 (.D(DW), .en(pull_resistor_8_node), .Q(register_8_q), .clk(in_1), .clr(in_2));
  Register_part #(.width(16)) register_9 (.D(DW), .en(pull_resistor_9_node), .Q(register_9_q), .clk(in_1), .clr(in_2));
  Register_part #(.width(16)) register_10 (
    .D(DW), .en(pull_resistor_10_node), .Q(register_10_q), .clk(in_1), .clr(in_2));
  Register_part #(.width(16)) register_11 (
    .D(DW), .en(pull_resistor_11_node), .Q(register_11_q), .clk(in_1), .clr(in_2));
  Register_part #(.width(16)) register_12 (
    .D(DW), .en(pull_resistor_12_node), .Q(register_12_q), .clk(in_1), .clr(in_2));
  Register_part #(.width(16)) register_13 (
    .D(DW), .en(pull_resistor_13_node), .Q(register_13_q), .clk(in_1), .clr(in_2));
  REG_IP reg_ip_1 (.in_1(DW), .in_2(pull_resistor_14_node), .in_3(in_1), .in_4(in_2), .out_5(out_12));
  Reg_SP reg_sp_1 (.in_1(DW), .in_2(pull_resistor_15_node), .in_3(in_1), .in_4(in_2), .out_5(reg_sp_1_out_5));
  Reg_Flags reg_flags_1 (
    .Data_In(DW), .Control(Control_Flags), .Enable(pull_resistor_16_node), .Clock(in_1), .Res(in_2),
    .Data_Out(FLAGS), .Data_In_Alu(Data_Flags));
  assign A = decoder_3_out0 ? register_1_q : 16'bz;  // Controlled_Buffer controlled_buffer_1
  assign B = decoder_2_out0 ? register_1_q : 16'bz;  // Controlled_Buffer controlled_buffer_2
  assign A = decoder_3_out1 ? register_2_q : 16'bz;  // Controlled_Buffer controlled_buffer_3
  assign B = decoder_2_out1 ? register_2_q : 16'bz;  // Controlled_Buffer controlled_buffer_4
  assign A = decoder_3_out2 ? register_3_q : 16'bz;  // Controlled_Buffer controlled_buffer_5
  assign B = decoder_2_out2 ? register_3_q : 16'bz;  // Controlled_Buffer controlled_buffer_6
  assign A = decoder_3_out3 ? register_4_q : 16'bz;  // Controlled_Buffer controlled_buffer_7
  assign B = decoder_2_out3 ? register_4_q : 16'bz;  // Controlled_Buffer controlled_buffer_8
  assign A = decoder_3_out4 ? register_5_q : 16'bz;  // Controlled_Buffer controlled_buffer_9
  assign B = decoder_2_out4 ? register_5_q : 16'bz;  // Controlled_Buffer controlled_buffer_10
  assign A = decoder_3_out5 ? register_6_q : 16'bz;  // Controlled_Buffer controlled_buffer_11
  assign B = decoder_2_out5 ? register_6_q : 16'bz;  // Controlled_Buffer controlled_buffer_12
  assign A = decoder_3_out6 ? register_7_q : 16'bz;  // Controlled_Buffer controlled_buffer_13
  assign B = decoder_2_out6 ? register_7_q : 16'bz;  // Controlled_Buffer controlled_buffer_14
  assign A = decoder_3_out7 ? register_8_q : 16'bz;  // Controlled_Buffer controlled_buffer_15
  assign B = decoder_2_out7 ? register_8_q : 16'bz;  // Controlled_Buffer controlled_buffer_16
  assign A = decoder_3_out8 ? register_9_q : 16'bz;  // Controlled_Buffer controlled_buffer_17
  assign B = decoder_2_out8 ? register_9_q : 16'bz;  // Controlled_Buffer controlled_buffer_18
  assign A = decoder_3_out9 ? register_10_q : 16'bz;  // Controlled_Buffer controlled_buffer_19
  assign B = decoder_2_out9 ? register_10_q : 16'bz;  // Controlled_Buffer controlled_buffer_20
  assign A = decoder_3_out10 ? register_11_q : 16'bz;  // Controlled_Buffer controlled_buffer_21
  assign B = decoder_2_out10 ? register_11_q : 16'bz;  // Controlled_Buffer controlled_buffer_22
  assign A = decoder_3_out11 ? register_12_q : 16'bz;  // Controlled_Buffer controlled_buffer_23
  assign B = decoder_2_out11 ? register_12_q : 16'bz;  // Controlled_Buffer controlled_buffer_24
  assign A = decoder_3_out12 ? register_13_q : 16'bz;  // Controlled_Buffer controlled_buffer_25
  assign B = decoder_2_out12 ? register_13_q : 16'bz;  // Controlled_Buffer controlled_buffer_26
  assign A = decoder_3_out13 ? out_12 : 16'bz;  // Controlled_Buffer controlled_buffer_27
  assign B = decoder_2_out13 ? out_12 : 16'bz;  // Controlled_Buffer controlled_buffer_28
  assign A = decoder_3_out14 ? reg_sp_1_out_5 : 16'bz;  // Controlled_Buffer controlled_buffer_29
  assign B = decoder_2_out14 ? reg_sp_1_out_5 : 16'bz;  // Controlled_Buffer controlled_buffer_30
  assign A = decoder_3_out15 ? FLAGS : 16'bz;  // Controlled_Buffer controlled_buffer_31
  assign B = decoder_2_out15 ? FLAGS : 16'bz;  // Controlled_Buffer controlled_buffer_32
endmodule

module ALU (
  input  Ci,
  input  [15:0] A,
  input  [15:0] B,
  input  [3:0] ALU_OP,
  output [15:0] out_5,
  output [15:0] FLAGS_C,
  output [15:0] FLAGS_D
);

  wire adder_1_cout, and_1_out, and_5_out, and_6_out, not_2_out, not_3_out, not_4_out, not_5_out, not_6_out,
       or_1_out, xor_1_out;
  wire [15:0] adder_1_out, and_4_out, multiplexer_1_out, not_1_out, or_2_out, shifter_1_out, shifter_2_out,
       shifter_3_out, xor_3_out;

  or or_1 (or_1_out, Ci, ALU_OP[2]);
  and and_1 (and_1_out, or_1_out, ALU_OP[0]);
  assign not_1_out = ~B;  // NOT_Gate not_1, 16 bits wide
  xor xor_1 (xor_1_out, and_1_out, ALU_OP[1]);
  Multiplexer #(.width(16)) multiplexer_1 (
    .in0(B), .in1(not_1_out), .out(multiplexer_1_out), .sel(ALU_OP[1]), .en(1'b1));
  not not_2 (not_2_out, ALU_OP[3]);
  not not_3 (not_3_out, ALU_OP[2]);
  and and_2 (FLAGS_C[3], not_2_out, not_3_out);
  and and_3 (FLAGS_C[0], not_2_out, not_3_out, ALU_OP[0]);
  Adder #(.width(16)) adder_1 (.a(A), .b(multiplexer_1_out), .out(adder_1_out), .cin(xor_1_out), .cout(adder_1_cout));
  xor xor_2 (FLAGS_D[0], adder_1_cout, ALU_OP[1]);
  assign and_4_out = A & B;  // AND_Gate and_4, 16 bits wide
  assign or_2_out = A | B;  // OR_Gate or_2, 16 bits wide
  assign xor_3_out = A ^ B;  // XOR_Gate xor_3, 16 bits wide
  Shifter #(.width(16), .shift("lr")) shifter_1 (.in(A), .\dist (B[3:0]), .out(shifter_1_out));
  Shifter #(.width(16)) shifter_2 (.in(A), .\dist (B[3:0]), .out(shifter_2_out));
  Shifter #(.width(16), .shift("rl")) shifter_3 (.in(A), .\dist (B[3:0]), .out(shifter_3_out));
  not not_4 (not_4_out, A[15]);
  not not_5 (not_5_out, B[15]);
  not not_6 (not_6_out, FLAGS_D[2]);
  and and_5 (and_5_out, B[15], not_4_out, FLAGS_D[2]);
  and and_6 (and_6_out, not_5_out, A[15], not_6_out);
  or or_3 (FLAGS_D[3], and_5_out, and_6_out);
  Hex_Digit_Display hex_digit_display_1 (.value(ALU_OP));  // open: dp
  Multiplexer #(.select(4), .width(16)) multiplexer_2 (
    .in0(adder_1_out), .in1(adder_1_out), .in2(adder_1_out), .in3(adder_1_out), .in4(and_4_out),
    .in5(or_2_out), .in6(xor_3_out), .in7(adder_1_out), .in8(shifter_1_out), .in9(shifter_2_out),
    .in10(shifter_3_out), .in11({16{1'b0}}), .in12({16{1'b0}}), .in13({16{1'b0}}), .in14({16{1'b0}}),
    .in15({16{1'b0}}), .out({FLAGS_D[2], out_5[14:0]}), .sel(ALU_OP), .en(1'b1));
  Comparator #(.width(16)) comparator_1 (
    .a({FLAGS_D[2], out_5[14:0]}), .b({16{1'b0}}), .eq(FLAGS_D[1]));  // open: gt, lt

  assign {FLAGS_C[15:4], FLAGS_C[2:1]} = {{12{1'b0}}, FLAGS_C[3], 1'b1};
  assign FLAGS_D[15:4] = {12{1'b0}};
  assign out_5[15] = FLAGS_D[2];
endmodule

module Control_Unit (
  input  [15:0] OP_1,
  input  [15:0] OP_2,
  input  [15:0] FLAGS,
  input  INT,
  input  INTR,
  input  CLOCK,
  input  RES,
  output D1,
  output D2,
  output EW,
  output IP,
  output FLAGS_W,
  output OP_r1,
  output OP_r2,
  output DATA,
  output [1:0] MUX_DW,
  output [1:0] MUX_B,
  output [1:0] MUX_Address,
  output Mem_R,
  output [3:0] ALU_OP,
  output Mem_W,
  output [1:0] MUX_AW,
  output MUX_DATA,
  output ALU_OUT,
  output MUX_OP2,
  output MFD,
  output MFC,
  output [15:0] FD,
  output [15:0] FC,
  output out_30,
  output INTA,
  output ReadInt,
  output MUX_A
);

  wire _11_out, and_2_out, and_3_out, and_4_out, and_5_out, and_6_out, and_7_out, and_8_out, and_9_out,
       and_11_out, and_12_out, and_13_out, and_14_out, and_15_out, and_16_out, and_17_out, and_18_out,
       and_19_out, and_20_out, and_21_out, and_22_out, and_23_out, and_24_out, decoder_1_out0,
       decoder_1_out2, decoder_1_out4, decoder_1_out5, decoder_1_out6, decoder_1_out7, decoder_1_out8,
       decoder_1_out12, decoder_1_out13, decoder_1_out16, decoder_1_out20, decoder_1_out21, decoder_1_out24,
       decoder_1_out25, decoder_1_out28, INT_t, not_1_out, not_2_out, not_3_out, not_4_out, not_5_out,
       not_6_out, not_7_out, not_8_out, not_9_out, not_10_out, not_11_out, not_12_out, not_13_out, or_1_out,
       or_2_out, or_8_out, or_9_out, or_10_out, or_11_out, xnor_1_out;
  wire [1:0] or_27_out;
  wire [1:1] or_28_out;
  wire [4:0] multiplexer_1_out, or_7_out, register_1_q;

  not not_1 (not_1_out, OP_1[11]);
  not not_2 (not_2_out, OP_1[10]);
  or or_1 (or_1_out, FLAGS[0], FLAGS[1]);
  not not_3 (not_3_out, OP_1[8]);
  not not_4 (not_4_out, OP_1[9]);
  not not_5 (not_5_out, FLAGS[1]);
  xnor xnor_1 (xnor_1_out, FLAGS[2], FLAGS[3]);
  not not_6 (not_6_out, INT_t);
  not not_7 (not_7_out, FLAGS[15]);
  and and_1 (INTA, INTR, not_7_out, not_6_out);
  S_R_Flip_Flop s_r_ff_1 (.S(INT), .clk(CLOCK), .R(FC[15]), .Q(INT_t), .reset(RES), .en(1'b1));  // open: Qn, preset
  and and_2 (and_2_out, not_3_out, not_4_out, not_2_out, not_1_out);
  and and_3 (and_3_out, not_4_out, not_2_out, not_1_out, OP_1[8], FLAGS[1]);
  and and_4 (and_4_out, not_5_out, OP_1[9], not_3_out, not_2_out, not_1_out);
  and and_5 (and_5_out, OP_1[8], OP_1[9], FLAGS[0], not_2_out, not_1_out);
  and and_6 (and_6_out, OP_1[10], OP_1[8], not_4_out, not_5_out, not_1_out, xnor_1_out);
  and and_7 (and_7_out, OP_1[9], OP_1[10], not_3_out, not_1_out, xnor_1_out);
  and and_8 (and_8_out, OP_1[10], not_4_out, not_3_out, or_1_out, not_1_out);
  and and_9 (and_9_out, not_10_out, not_9_out, decoder_1_out2, OP_1[2], OP_1[3]);
  or or_2 (or_2_out, and_2_out, and_3_out, and_4_out, and_5_out, and_8_out, and_6_out, and_7_out);
  and and_10 (ReadInt, INT_t, decoder_1_out0);
  and and_11 (and_11_out, OP_1[3], OP_1[2], OP_1[1], OP_1[0], decoder_1_out2);
  or or_3 (or_7_out[4], and_11_out, and_12_out, and_19_out, and_18_out, and_17_out, decoder_1_out24, decoder_1_out20);
  or or_4 (or_7_out[3], decoder_1_out12, and_18_out, and_9_out, or_9_out, _11_out);
  or or_5 (or_7_out[2], decoder_1_out12, decoder_1_out20, and_12_out, and_19_out, and_16_out, decoder_1_out5, _11_out);
  or or_6 (or_7_out[1], and_16_out, and_13_out, or_11_out, and_14_out, OP_r2);
  or or_7 (or_7_out[0], decoder_1_out12, decoder_1_out20, decoder_1_out24, and_16_out, and_13_out, or_8_out, and_11_out);
  Multiplexer #(.width(5)) multiplexer_1 (
    .in0(or_7_out), .in1({2'b00, OP_1[3:1]}), .out(multiplexer_1_out), .sel(ALU_OUT), .en(1'b1));
  and _11 (_11_out, not_10_out, OP_1[1], OP_1[2], OP_1[3], decoder_1_out2);
  and and_12 (and_12_out, OP_1[3], OP_1[2], not_9_out, OP_1[0], decoder_1_out2);
  not not_8 (not_8_out, OP_1[3]);
  not not_9 (not_9_out, OP_1[1]);
  not not_10 (not_10_out, OP_1[0]);
  not not_11 (not_11_out, OP_1[2]);
  and and_13 (and_13_out, OP_1[3], decoder_1_out2, not_11_out);
  or or_8 (or_8_out, and_15_out, decoder_1_out8);
  and and_14 (and_14_out, not_10_out, decoder_1_out0);
  and and_15 (and_15_out, OP_1[0], decoder_1_out0);
  and and_16 (and_16_out, not_8_out, not_11_out, OP_1[0], decoder_1_out2);
  or or_9 (or_9_out, and_19_out, or_10_out);
  not not_12 (not_12_out, CLOCK);
  and and_17 (and_17_out, not_8_out, OP_1[2], not_9_out, decoder_1_out2);
  or or_10 (or_10_out, decoder_1_out24, decoder_1_out8);
  buf or_11 (or_11_out, decoder_1_out5);  // OR_Gate
  Decoder #(.select(5)) decoder_1 (
    .out0(decoder_1_out0), .out1(OP_r2), .out2(decoder_1_out2), .out3(ALU_OUT), .out4(decoder_1_out4),
    .out5(decoder_1_out5), .out6(decoder_1_out6), .out7(decoder_1_out7), .out8(decoder_1_out8),
    .out9(FC[15]), .out12(decoder_1_out12), .out13(decoder_1_out13), .out16(decoder_1_out16), .out17(out_30),
    .out20(decoder_1_out20), .out21(decoder_1_out21), .out24(decoder_1_out24), .out25(decoder_1_out25),
    .out28(decoder_1_out28), .sel(register_1_q), .en(1'b1));  // open: out10, out11, out14, out15, out18, out19, out22, out23, out26, out27, out29, out30, out31
  Register_part #(.width(5)) register_1 (
    .D(multiplexer_1_out), .Q(register_1_q), .clk(not_12_out), .clr(RES));  // open: en
  and and_18 (and_18_out, not_8_out, not_11_out, decoder_1_out2, OP_1[1], not_10_out);
  and and_19 (and_19_out, not_8_out, OP_1[2], OP_1[1], decoder_1_out2);
  buf or_12 (D1, decoder_1_out2);  // OR_Gate
  buf or_13 (OP_r1, decoder_1_out0);  // OR_Gate
  or or_14 (IP, decoder_1_out0, OP_r2, and_20_out);
  and and_20 (and_20_out, decoder_1_out28, or_2_out);
  buf or_15 (D2, decoder_1_out2);  // OR_Gate
  and and_21 (and_21_out, not_13_out, IP);
  not not_13 (not_13_out, INT_t);
  or or_16 (DATA, decoder_1_out5, decoder_1_out24, decoder_1_out12);
  or or_17 (EW, and_21_out, decoder_1_out13, decoder_1_out21, decoder_1_out24, decoder_1_out16, decoder_1_out6, decoder_1_out7, decoder_1_out25, decoder_1_out20, decoder_1_out12, FC[15], decoder_1_out8);
  or or_18 (MUX_DW[1], decoder_1_out21, 1'b0, FC[15]);
  or or_19 (MUX_DW[0], decoder_1_out8, decoder_1_out12, decoder_1_out21, decoder_1_out16, decoder_1_out7, decoder_1_out24, decoder_1_out20, FC[15], IP);
  or or_20 (MUX_A, decoder_1_out8, decoder_1_out12, decoder_1_out24, decoder_1_out7, ALU_OUT, decoder_1_out16, decoder_1_out28, decoder_1_out20);
  or or_21 (MUX_B[1], ALU_OUT, and_22_out, decoder_1_out12, decoder_1_out28);
  and and_22 (and_22_out, decoder_1_out7, OP_1[1]);
  or or_22 (MUX_B[0], decoder_1_out8, and_24_out, decoder_1_out16, OP_r2, decoder_1_out0, and_23_out, decoder_1_out24, decoder_1_out20);
  and and_23 (and_23_out, ALU_OUT, not_10_out);
  and and_24 (and_24_out, not_10_out, decoder_1_out28);
  or or_23 (MUX_Address[1], decoder_1_out4, decoder_1_out24, decoder_1_out5, decoder_1_out12);
  or or_24 (MUX_Address[0], decoder_1_out8, decoder_1_out20, decoder_1_out4, decoder_1_out5, decoder_1_out16);
  or or_25 (Mem_R, decoder_1_out24, decoder_1_out0, OP_r2, decoder_1_out5, decoder_1_out12);
  or or_26 (or_27_out[1], decoder_1_out8, decoder_1_out20, decoder_1_out16, OP_1[1]);
  Multiplexer #(.select(2), .width(4)) multiplexer_2 (
    .in0(4'b0000), .in1(OP_2[15:12]), .in2({2'b00, or_28_out[1], 1'b0}), .in3(OP_1[11:8]), .out(ALU_OP),
    .sel(or_27_out), .en(1'b1));
  buf or_27 (or_27_out[0], decoder_1_out7);  // OR_Gate
  or or_28 (or_28_out[1], decoder_1_out8, decoder_1_out16, decoder_1_out20);
  or or_29 (Mem_W, decoder_1_out16, decoder_1_out4, decoder_1_out20, decoder_1_out8);
  or or_30 (MUX_AW[1], decoder_1_out8, decoder_1_out12, IP);
  or or_31 (MUX_AW[0], FC[15], decoder_1_out13, decoder_1_out21, decoder_1_out24, IP);
  and and_25 (MUX_DATA, decoder_1_out16, OP_1[0]);
  or or_32 (MUX_OP2, FC[15], decoder_1_out12);
  or or_33 (FLAGS_W, decoder_1_out7, FC[15]);

  assign FC[14:0] = {15{1'b0}};
  assign FD = {FC[15], {15{1'b0}}};
  assign MFC = FC[15];
  assign MFD = FC[15];

  // Notes on the sheet:
  //   ALU
  //   INT
  //   RET
  //   PUSH
  //   CALL
  //   POP
  //   JMP
endmodule

module Reg_Flags (
  input  [15:0] Data_In,
  input  [15:0] Data_In_Alu,
  input  [15:0] Control,
  input  Enable,
  input  Clock,
  input  Res,
  output [15:0] Data_Out
);

  wire not_1_out, or_1_out, or_2_out, or_3_out, or_4_out, or_5_out, or_6_out, or_7_out, or_8_out, or_9_out,
       or_10_out, or_11_out, or_12_out, or_13_out, or_14_out, or_15_out, or_16_out;
  wire [15:0] multiplexer_1_out;

  not not_1 (not_1_out, Enable);
  Multiplexer #(.width(16)) multiplexer_1 (
    .in0(Data_In), .in1(Data_In_Alu), .out(multiplexer_1_out), .sel(not_1_out), .en(1'b1));
  or or_1 (or_1_out, Enable, Control[0]);
  or or_2 (or_2_out, Control[15], Enable);
  or or_3 (or_3_out, Enable, Control[1]);
  or or_4 (or_4_out, Enable, Control[2]);
  or or_5 (or_5_out, Control[13], Enable);
  or or_6 (or_6_out, Control[14], Enable);
  or or_7 (or_7_out, Enable, Control[3]);
  or or_8 (or_8_out, Enable, Control[4]);
  or or_9 (or_9_out, Control[11], Enable);
  or or_10 (or_10_out, Control[12], Enable);
  or or_11 (or_11_out, Enable, Control[5]);
  or or_12 (or_12_out, Enable, Control[6]);
  or or_13 (or_13_out, Control[9], Enable);
  or or_14 (or_14_out, Control[10], Enable);
  or or_15 (or_15_out, Enable, Control[7]);
  or or_16 (or_16_out, Control[8], Enable);
  Register_part #(.width(1)) register_1 (
    .D(multiplexer_1_out[0]), .en(or_1_out), .Q(Data_Out[0]), .clk(Clock), .clr(Res));
  Register_part #(.width(1)) register_2 (
    .D(multiplexer_1_out[1]), .en(or_3_out), .Q(Data_Out[1]), .clk(Clock), .clr(Res));
  Register_part #(.width(1)) register_3 (
    .D(multiplexer_1_out[2]), .en(or_4_out), .Q(Data_Out[2]), .clk(Clock), .clr(Res));
  Register_part #(.width(1)) register_4 (
    .D(multiplexer_1_out[3]), .en(or_7_out), .Q(Data_Out[3]), .clk(Clock), .clr(Res));
  Register_part #(.width(1)) register_5 (
    .D(multiplexer_1_out[4]), .en(or_8_out), .Q(Data_Out[4]), .clk(Clock), .clr(Res));
  Register_part #(.width(1)) register_6 (
    .D(multiplexer_1_out[5]), .en(or_11_out), .Q(Data_Out[5]), .clk(Clock), .clr(Res));
  Register_part #(.width(1)) register_7 (
    .D(multiplexer_1_out[6]), .en(or_12_out), .Q(Data_Out[6]), .clk(Clock), .clr(Res));
  Register_part #(.width(1)) register_8 (
    .D(multiplexer_1_out[7]), .en(or_15_out), .Q(Data_Out[7]), .clk(Clock), .clr(Res));
  Register_part #(.width(1)) register_9 (
    .D(multiplexer_1_out[8]), .en(or_16_out), .Q(Data_Out[8]), .clk(Clock), .clr(Res));
  Register_part #(.width(1)) register_10 (
    .D(multiplexer_1_out[9]), .en(or_13_out), .Q(Data_Out[9]), .clk(Clock), .clr(Res));
  Register_part #(.width(1)) register_11 (
    .D(multiplexer_1_out[10]), .en(or_14_out), .Q(Data_Out[10]), .clk(Clock), .clr(Res));
  Register_part #(.width(1)) register_12 (
    .D(multiplexer_1_out[11]), .en(or_9_out), .Q(Data_Out[11]), .clk(Clock), .clr(Res));
  Register_part #(.width(1)) register_13 (
    .D(multiplexer_1_out[12]), .en(or_10_out), .Q(Data_Out[12]), .clk(Clock), .clr(Res));
  Register_part #(.width(1)) register_14 (
    .D(multiplexer_1_out[13]), .en(or_5_out), .Q(Data_Out[13]), .clk(Clock), .clr(Res));
  Register_part #(.width(1)) register_15 (
    .D(multiplexer_1_out[14]), .en(or_6_out), .Q(Data_Out[14]), .clk(Clock), .clr(Res));
  Register_part #(.width(1)) register_16 (
    .D(multiplexer_1_out[15]), .en(or_2_out), .Q(Data_Out[15]), .clk(Clock), .clr(Res));
endmodule

module Reg_SP (
  input  [15:0] in_1,
  input  in_2,
  input  in_3,
  input  in_4,
  output [15:0] out_5
);

  wire or_1_out;
  wire [15:0] multiplexer_1_out;

  or or_1 (or_1_out, in_2, in_4);
  Multiplexer #(.width(16)) multiplexer_1 (
    .in0(in_1), .in1({16{1'b1}}), .out(multiplexer_1_out), .sel(in_4), .en(1'b1));
  Register_part #(.width(16)) register_1 (.D(multiplexer_1_out), .en(or_1_out), .Q(out_5), .clk(in_3));  // open: clr
endmodule

module IC (
  input  _0,
  input  _1,
  input  _2,
  input  _3,
  input  INTA,
  input  CLK,
  input  W,
  input  R,
  input  Reset,
  output [15:0] DATA,
  output INT,
  output INTR
);

  wire demultiplexer_1_out14, demultiplexer_1_out15, priority_encoder_1_en_out, priority_encoder_1_gs,
       s_r_ff_1_q, s_r_ff_2_q;
  wire [15:12] priority_encoder_1_out;

  or or_1 (INTR, _3, _2, s_r_ff_2_q, s_r_ff_1_q);
  and and_1 (INT, INTA, INTR);
  S_R_Flip_Flop s_r_ff_1 (
    .S(_0), .clk(CLK), .R(demultiplexer_1_out15), .Q(s_r_ff_1_q), .reset(Reset), .en(1'b1));  // open: Qn, preset
  S_R_Flip_Flop s_r_ff_2 (
    .S(_1), .clk(CLK), .R(demultiplexer_1_out14), .Q(s_r_ff_2_q), .reset(Reset), .en(1'b1));  // open: Qn, preset
  Priority_Encoder #(.select(4), .disabled(0)) priority_encoder_1 (
    .in0(1'b0), .in1(1'b0), .in2(1'b0), .in3(1'b0), .in4(1'b0), .in5(1'b0), .in6(1'b0), .in7(1'b0),
    .in8(1'b0), .in9(1'b0), .in10(1'b0), .in11(1'b0), .in12(1'b0), .in13(1'b0), .in14(s_r_ff_2_q),
    .in15(s_r_ff_1_q), .out(priority_encoder_1_out), .gs(priority_encoder_1_gs),
    .en_out(priority_encoder_1_en_out));  // open: en_in
  Demultiplexer #(.select(4), .disabled(0)) demultiplexer_1 (
    .out14(demultiplexer_1_out14), .out15(demultiplexer_1_out15), .in(1'b1), .sel(priority_encoder_1_out),
    .en(R));  // open: out0, out1, out2, out3, out4, out5, out6, out7, out8, out9, out10, out11, out12, out13
  Pull_Resistor pull_resistor_1 (.node(priority_encoder_1_out));
  assign DATA = R ? {priority_encoder_1_out, 12'hdec} : 16'bz;  // Controlled_Buffer controlled_buffer_1
endmodule

module MC (
  input  ReadInt,
  input  [15:0] ADRESS,
  input  EW,
  input  ER,
  output EW1,
  output ER1,
  output EW2,
  output ER2,
  output EWK,
  output ERK,
  output EW0,
  output ER0
);

  wire and_2_out, comparator_1_gt, comparator_2_lt, comparator_4_eq, not_2_out, not_3_out;

  Comparator #(.width(16), .mode("unsigned")) comparator_1 (
    .a(ADRESS), .b(16'h3f), .gt(comparator_1_gt));  // open: eq, lt
  Comparator #(.width(16), .mode("unsigned")) comparator_2 (
    .a(ADRESS), .b(16'h50), .lt(comparator_2_lt));  // open: gt, eq
  // NOT_Gate not_1 has open pins: in=and_2_out, out=open
  buf and_1 (EW0, EW);  // AND_Gate
  and and_2 (and_2_out, comparator_1_gt, comparator_2_lt);
  not not_2 (not_2_out, ReadInt);
  and and_3 (ER0, 1'b1, ER, not_2_out, not_3_out);
  Comparator #(.width(16), .mode("unsigned")) comparator_3 (.a(ADRESS), .b(16'h7f));  // open: gt, eq, lt
  not not_3 (not_3_out, comparator_4_eq);
  and and_4 (EW1, 1'b0, EW);
  and and_5 (ER1, ReadInt, ER);
  and and_6 (EW2, and_2_out, EW);
  and and_7 (ER2, 1'b0, ER);
  Comparator #(.width(16), .mode("unsigned")) comparator_4 (
    .a(ADRESS), .b(16'h1c), .eq(comparator_4_eq));  // open: gt, lt
  and and_8 (EWK, EW, 1'b0);
  and and_9 (ERK, comparator_4_eq, ER);
endmodule

module REG_IP (
  input  [15:0] in_1,
  input  in_2,
  input  in_3,
  input  in_4,
  output [15:0] out_5
);

  wire or_1_out;
  wire [15:0] multiplexer_1_out;

  or or_1 (or_1_out, in_2, in_4);
  Multiplexer #(.width(16)) multiplexer_1 (.in0(in_1), .in1(16'h80), .out(multiplexer_1_out), .sel(in_4), .en(1'b1));
  Register_part #(.width(16)) register_1 (.D(multiplexer_1_out), .en(or_1_out), .Q(out_5), .clk(in_3));  // open: clr
endmodule

module LED (
  input  CLOCK,
  input  RESET,
  input  [15:0] DATA,
  input  EW,
  input  [3:0] ADDRES,
  output [15:0] out_6,
  output [15:0] out_7,
  output [15:0] out_8,
  output [15:0] out_9,
  output [15:0] out_10,
  output [15:0] out_11,
  output [15:0] out_12,
  output [15:0] out_13,
  output [15:0] out_14,
  output [15:0] out_15,
  output [15:0] out_16,
  output [15:0] out_17,
  output [15:0] out_18,
  output [15:0] out_19,
  output [15:0] out_20,
  output [15:0] out_21
);

  wire demultiplexer_1_out0, demultiplexer_1_out1, demultiplexer_1_out2, demultiplexer_1_out3,
       demultiplexer_1_out4, demultiplexer_1_out5, demultiplexer_1_out6, demultiplexer_1_out7,
       demultiplexer_1_out8, demultiplexer_1_out9, demultiplexer_1_out10, demultiplexer_1_out11,
       demultiplexer_1_out12, demultiplexer_1_out13, demultiplexer_1_out14, demultiplexer_1_out15;

  Demultiplexer #(.select(4)) demultiplexer_1 (
    .out0(demultiplexer_1_out0), .out1(demultiplexer_1_out1), .out2(demultiplexer_1_out2),
    .out3(demultiplexer_1_out3), .out4(demultiplexer_1_out4), .out5(demultiplexer_1_out5),
    .out6(demultiplexer_1_out6), .out7(demultiplexer_1_out7), .out8(demultiplexer_1_out8),
    .out9(demultiplexer_1_out9), .out10(demultiplexer_1_out10), .out11(demultiplexer_1_out11),
    .out12(demultiplexer_1_out12), .out13(demultiplexer_1_out13), .out14(demultiplexer_1_out14),
    .out15(demultiplexer_1_out15), .in(EW), .sel(ADDRES), .en(1'b1));
  Register_part #(.width(16)) register_1 (.D(DATA), .en(demultiplexer_1_out0), .Q(out_6), .clk(CLOCK), .clr(RESET));
  Register_part #(.width(16)) register_2 (.D(DATA), .en(demultiplexer_1_out1), .Q(out_7), .clk(CLOCK), .clr(RESET));
  Register_part #(.width(16)) register_3 (.D(DATA), .en(demultiplexer_1_out2), .Q(out_8), .clk(CLOCK), .clr(RESET));
  Register_part #(.width(16)) register_4 (.D(DATA), .en(demultiplexer_1_out3), .Q(out_9), .clk(CLOCK), .clr(RESET));
  Register_part #(.width(16)) register_5 (.D(DATA), .en(demultiplexer_1_out4), .Q(out_10), .clk(CLOCK), .clr(RESET));
  Register_part #(.width(16)) register_6 (.D(DATA), .en(demultiplexer_1_out5), .Q(out_11), .clk(CLOCK), .clr(RESET));
  Register_part #(.width(16)) register_7 (.D(DATA), .en(demultiplexer_1_out6), .Q(out_12), .clk(CLOCK), .clr(RESET));
  Register_part #(.width(16)) register_8 (.D(DATA), .en(demultiplexer_1_out7), .Q(out_13), .clk(CLOCK), .clr(RESET));
  Register_part #(.width(16)) register_9 (.D(DATA), .en(demultiplexer_1_out8), .Q(out_14), .clk(CLOCK), .clr(RESET));
  Register_part #(.width(16)) register_10 (.D(DATA), .en(demultiplexer_1_out9), .Q(out_15), .clk(CLOCK), .clr(RESET));
  Register_part #(.width(16)) register_11 (.D(DATA), .en(demultiplexer_1_out10), .Q(out_16), .clk(CLOCK), .clr(RESET));
  Register_part #(.width(16)) register_12 (.D(DATA), .en(demultiplexer_1_out11), .Q(out_17), .clk(CLOCK), .clr(RESET));
  Register_part #(.width(16)) register_13 (.D(DATA), .en(demultiplexer_1_out12), .Q(out_18), .clk(CLOCK), .clr(RESET));
  Register_part #(.width(16)) register_14 (.D(DATA), .en(demultiplexer_1_out13), .Q(out_19), .clk(CLOCK), .clr(RESET));
  Register_part #(.width(16)) register_15 (.D(DATA), .en(demultiplexer_1_out14), .Q(out_20), .clk(CLOCK), .clr(RESET));
  Register_part #(.width(16)) register_16 (.D(DATA), .en(demultiplexer_1_out15), .Q(out_21), .clk(CLOCK), .clr(RESET));
endmodule

module Keyboard (
  input  in_1,
  input  in_2,
  input  in_3,
  input  in_4,
  input  Clock,
  input  Res,
  input  ER,
  output [15:0] Data,
  output INT
);

  wire d_ff_1_qn, or_1_out;
  wire [15:0] register_1_q;

  or or_1 (or_1_out, in_1, in_2, in_3, in_4);
  D_Flip_Flop d_ff_1 (.clk(or_1_out), .D(or_1_out), .Q(INT), .Qn(d_ff_1_qn), .en(1'b1), .reset(ER));  // open: preset
  Register_part #(.width(16)) register_1 (
    .D({{12{1'b0}}, in_4, in_3, in_2, in_1}), .Q(register_1_q), .clk(INT), .clr(Res));  // open: en
  assign Data = ER ? register_1_q : 16'bz;  // Controlled_Buffer controlled_buffer_1
endmodule

module q (
  input  A,
  input  B,
  input  A_2,
  input  B_2,
  output C,
  output C_2
);

  wire and_1_out, and_2_out, not_1_out, not_2_out;

  not not_1 (not_1_out, A);
  not not_2 (not_2_out, B);
  and and_1 (and_1_out, not_1_out, not_2_out);
  and and_2 (and_2_out, A, B);
  xnor xnor_1 (C_2, A_2, B_2);
  or or_1 (C, and_1_out, and_2_out);
endmodule
