// Logisim project processor.circ as structural Verilog: 9 circuits, main circuit main
module main (
  input  in_1,
  output [15:0] out_2
);

  wire button_1_out, CF, clock_1_out, control_unit_1__1, control_unit_1__2, control_unit_1__3,
       control_unit_1_e_op, control_unit_1_ew, control_unit_1_mux_a, control_unit_1_out_9,
       control_unit_1_out_10, control_unit_1_out_16, control_unit_1_out_17, MUX_ALU_OUT, or_1_out;
  wire [1:0] control_unit_1_mux_b, control_unit_1_mux_dw;
  wire [3:0] alu_1_out_6, alu_1_out_6_2, alu_1_out_6_3, alu_1_out_6_4, ALU_OP, register_2_q_2, register_3_q;
  wire [11:0] register_3_q_2;
  wire [15:0] alu_1_flags, ALU_OUT, multiplexer_1_out, multiplexer_2_out, multiplexer_3_out,
       multiplexer_4_out, NEXT_OP, OP, register_2_q, register_4_q, register_5_q, register_6_q, undriven,
       \регистры_1_a , \регистры_1_b ;
  wire [15:1] flags_1_out_5;

  Clock clock_1 (.out(clock_1_out));
  Button button_1 (.out(button_1_out));
  Register #(.width(16)) register_1 (.D(NEXT_OP), .en(or_1_out), .Q(OP), .clk(clock_1_out), .clr(button_1_out));
  Multiplexer #(.width(16)) multiplexer_1 (
    .in0(OP), .in1(ALU_OUT), .out(multiplexer_1_out), .sel(control_unit_1_out_9), .en(1'b1));
  buf or_1 (or_1_out, control_unit_1_e_op);  // OR_Gate
  RAM #(.addrWidth(16), .dataWidth(16), .bus("separate")) ram_1 (
    .addr(multiplexer_1_out), .din(register_6_q), .data(out_2), .str(control_unit_1_out_10), .sel(1'b1),
    .clk(clock_1_out), .ld(1'b1), .clr(in_1));
  Register #(.width(16)) register_2 (
    .D(out_2), .en(control_unit_1__1), .Q({register_2_q[15:8], register_2_q_2, register_2_q[3:0]}),
    .clk(clock_1_out), .clr(button_1_out));
  Register #(.width(16)) register_3 (
    .D(out_2), .en(control_unit_1__2), .Q({register_3_q_2, register_3_q}), .clk(clock_1_out),
    .clr(button_1_out));
  Register #(.width(16)) register_4 (
    .D(out_2), .en(control_unit_1__3), .Q(register_4_q), .clk(clock_1_out), .clr(button_1_out));
  Control_Unit control_unit_1 (
    .in_3(clock_1_out), .E_OP(control_unit_1_e_op), .out_9(control_unit_1_out_9),
    .out_10(control_unit_1_out_10), ._1(control_unit_1__1), ._2(control_unit_1__2), ._3(control_unit_1__3),
    .MUX_DW(control_unit_1_mux_dw), .EW(control_unit_1_ew), .out_16(control_unit_1_out_16),
    .out_17(control_unit_1_out_17), .MUX_B(control_unit_1_mux_b), .MUX_A(control_unit_1_mux_a),
    .COM_ALU(ALU_OP), .MUX_OP(MUX_ALU_OUT), .in_4(button_1_out),
    .in_1({register_2_q[15:8], register_2_q_2, register_2_q[3:0]}), .in_2({register_3_q_2, register_3_q}));  // open: out_20, BRANCH
  Hex_Digit_Display hex_digit_display_1 (.value(register_2_q[15:12]));  // open: dp
  Hex_Digit_Display hex_digit_display_2 (.value(register_2_q[11:8]));  // open: dp
  Multiplexer #(.select(2), .width(16)) multiplexer_2 (
    .in0(register_4_q), .in1(ALU_OUT), .in2(OP), .out(multiplexer_2_out), .sel(control_unit_1_mux_dw),
    .en(1'b1));  // open: in3
  \Регистры  \u_регистры_1  (
    .A1(register_2_q[11:8]), .A3(register_2_q_2), .DW(multiplexer_2_out), .A2(register_2_q[15:12]),
    .A(\регистры_1_a ), .B(\регистры_1_b ), .in_1(clock_1_out), .in_2(button_1_out), .in_4(control_unit_1_ew));
  Register #(.width(16)) register_5 (
    .D(\регистры_1_a ), .en(control_unit_1_out_16), .Q(register_5_q), .clk(clock_1_out), .clr(button_1_out));
  Register #(.width(16)) register_6 (
    .D(\регистры_1_b ), .en(control_unit_1_out_17), .Q(register_6_q), .clk(clock_1_out), .clr(button_1_out));
  Multiplexer #(.width(16)) multiplexer_3 (
    .in0(OP), .in1(register_5_q), .out(multiplexer_3_out), .sel(control_unit_1_mux_a), .en(1'b1));
  Multiplexer #(.select(2), .width(16)) multiplexer_4 (
    .in0(register_6_q), .in1(16'h1), .in2({register_3_q_2, register_3_q}),
    .in3({register_3_q_2, register_2_q_2}), .out(multiplexer_4_out), .sel(control_unit_1_mux_b), .en(1'b1));
  Hex_Digit_Display hex_digit_display_3 (.value(alu_1_out_6_4));  // open: dp
  ALU alu_1 (
    .A(multiplexer_3_out), .B(multiplexer_4_out), .ALU_OP(ALU_OP), .in_5(register_2_q[15:12]),
    .out_6({alu_1_out_6_4, alu_1_out_6_3, alu_1_out_6_2, alu_1_out_6}), .Ci(CF), .FLAGS(alu_1_flags));
  Hex_Digit_Display hex_digit_display_4 (.value(alu_1_out_6_3));  // open: dp
  Hex_Digit_Display hex_digit_display_5 (.value(alu_1_out_6_2));  // open: dp
  Hex_Digit_Display hex_digit_display_6 (.value(alu_1_out_6));  // open: dp
  Register #(.width(16)) register_7 (
    .D({alu_1_out_6_4, alu_1_out_6_3, alu_1_out_6_2, alu_1_out_6}), .en(1'b1), .Q(ALU_OUT),
    .clk(clock_1_out), .clr(button_1_out));
  Multiplexer #(.width(16)) multiplexer_5 (
    .in0({alu_1_out_6_4, alu_1_out_6_3, alu_1_out_6_2, alu_1_out_6}), .in1(ALU_OUT), .out(NEXT_OP),
    .sel(MUX_ALU_OUT), .en(1'b1));
  FLAGS flags_1 (
    .in_1(alu_1_flags), .in_2(undriven), .out_5({flags_1_out_5, CF}), .CLOCK(clock_1_out),
    .RESET(button_1_out));
endmodule

module \Регистры  (
  input  in_1,
  input  in_2,
  input  [3:0] A1,
  input  in_4,
  input  [3:0] A3,
  input  [15:0] DW,
  input  [3:0] A2,
  output [15:0] A,
  output [15:0] B
);

  wire decoder_2_out0, decoder_2_out1, decoder_2_out2, decoder_2_out3, decoder_2_out4, decoder_2_out5,
       decoder_2_out6, decoder_2_out7, decoder_2_out8, decoder_2_out9, decoder_2_out10, decoder_2_out11,
       decoder_2_out12, decoder_2_out13, decoder_2_out14, decoder_2_out15, decoder_3_out0, decoder_3_out1,
       decoder_3_out2, decoder_3_out3, decoder_3_out4, decoder_3_out5, decoder_3_out6, decoder_3_out7,
       decoder_3_out8, decoder_3_out9, decoder_3_out10, decoder_3_out11, decoder_3_out12, decoder_3_out13,
       decoder_3_out14, decoder_3_out15, pull_resistor_1_node, pull_resistor_2_node, pull_resistor_3_node,
       pull_resistor_4_node, pull_resistor_5_node, pull_resistor_6_node, pull_resistor_7_node,
       pull_resistor_8_node, pull_resistor_9_node, pull_resistor_10_node, pull_resistor_11_node,
       pull_resistor_12_node, pull_resistor_13_node, pull_resistor_14_node, pull_resistor_15_node,
       pull_resistor_16_node;
  wire [15:0] register_1_q, register_2_q, register_3_q, register_4_q, register_5_q, register_6_q,
       register_7_q, register_8_q, register_9_q, register_10_q, register_11_q, register_12_q, register_13_q,
       register_14_q, register_15_q, register_16_q;

  Pull_Resistor pull_resistor_1 (.node(pull_resistor_1_node));
  Pull_Resistor pull_resistor_2 (.node(pull_resistor_2_node));
  Pull_Resistor pull_resistor_3 (.node(pull_resistor_3_node));
  Pull_Resistor pull_resistor_4 (.node(pull_resistor_4_node));
  Pull_Resistor pull_resistor_5 (.node(pull_resistor_5_node));
  Pull_Resistor pull_resistor_6 (.node(pull_resistor_6_node));
  Pull_Resistor pull_resistor_7 (.node(pull_resistor_7_node));
  Pull_Resistor pull_resistor_8 (.node(pull_resistor_8_node));
  Pull_Resistor pull_resistor_9 (.node(pull_resistor_9_node));
  Pull_Resistor pull_resistor_10 (.node(pull_resistor_10_node));
  Pull_Resistor pull_resistor_11 (.node(pull_resistor_11_node));
  Pull_Resistor pull_resistor_12 (.node(pull_resistor_12_node));
  Pull_Resistor pull_resistor_13 (.node(pull_resistor_13_node));
  Pull_Resistor pull_resistor_14 (.node(pull_resistor_14_node));
  Pull_Resistor pull_resistor_15 (.node(pull_resistor_15_node));
  Pull_Resistor pull_resistor_16 (.node(pull_resistor_16_node));
  Decoder #(.select(4)) decoder_1 (
    .out0(pull_resistor_1_node), .out1(pull_resistor_2_node), .out2(pull_resistor_3_node),
    .out3(pull_resistor_4_node), .out4(pull_resistor_5_node), .out5(pull_resistor_6_node),
    .out6(pull_resistor_7_node), .out7(pull_resistor_8_node), .out8(pull_resistor_9_node),
    .out9(pull_resistor_10_node), .out10(pull_resistor_11_node), .out11(pull_resistor_12_node),
    .out12(pull_resistor_13_node), .out13(pull_resistor_14_node), .out14(pull_resistor_15_node),
    .out15(pull_resistor_16_node), .sel(A3), .en(in_4));
  Decoder #(.select(4)) decoder_2 (
    .out0(decoder_2_out0), .out1(decoder_2_out1), .out2(decoder_2_out2), .out3(decoder_2_out3),
    .out4(decoder_2_out4), .out5(decoder_2_out5), .out6(decoder_2_out6), .out7(decoder_2_out7),
    .out8(decoder_2_out8), .out9(decoder_2_out9), .out10(decoder_2_out10), .out11(decoder_2_out11),
    .out12(decoder_2_out12), .out13(decoder_2_out13), .out14(decoder_2_out14), .out15(decoder_2_out15),
    .sel(A2), .en(1'b1));
  Decoder #(.select(4)) decoder_3 (
    .out0(decoder_3_out0), .out1(decoder_3_out1), .out2(decoder_3_out2), .out3(decoder_3_out3),
    .out4(decoder_3_out4), .out5(decoder_3_out5), .out6(decoder_3_out6), .out7(decoder_3_out7),
    .out8(decoder_3_out8), .out9(decoder_3_out9), .out10(decoder_3_out10), .out11(decoder_3_out11),
    .out12(decoder_3_out12), .out13(decoder_3_out13), .out14(decoder_3_out14), .out15(decoder_3_out15),
    .sel(A1), .en(1'b1));
  Register #(.width(16)) register_1 (.D(DW), .en(pull_resistor_1_node), .Q(register_1_q), .clk(in_1), .clr(in_2));
  Register #(.width(16)) register_2 (.D(DW), .en(pull_resistor_2_node), .Q(register_2_q), .clk(in_1), .clr(in_2));
  Register #(.width(16)) register_3 (.D(DW), .en(pull_resistor_3_node), .Q(register_3_q), .clk(in_1), .clr(in_2));
  Register #(.width(16)) register_4 (.D(DW), .en(pull_resistor_4_node), .Q(register_4_q), .clk(in_1), .clr(in_2));
  Register #(.width(16)) register_5 (.D(DW), .en(pull_resistor_5_node), .Q(register_5_q), .clk(in_1), .clr(in_2));
  Register #(.width(16)) register_6 (.D(DW), .en(pull_resistor_6_node), .Q(register_6_q), .clk(in_1), .clr(in_2));
  Register #(.width(16)) register_7 (.D(DW), .en(pull_resistor_7_node), .Q(register_7_q), .clk(in_1), .clr(in_2));
  Register #(.width(16)) register_8 (.D(DW), .en(pull_resistor_8_node), .Q(register_8_q), .clk(in_1), .clr(in_2));
  Register #(.width(16)) register_9 (.D(DW), .en(pull_resistor_9_node), .Q(register_9_q), .clk(in_1), .clr(in_2));
  Register #(.width(16)) register_10 (.D(DW), .en(pull_resistor_10_node), .Q(register_10_q), .clk(in_1), .clr(in_2));
  Register #(.width(16)) register_11 (.D(DW), .en(pull_resistor_11_node), .Q(register_11_q), .clk(in_1), .clr(in_2));
  Register #(.width(16)) register_12 (.D(DW), .en(pull_resistor_12_node), .Q(register_12_q), .clk(in_1), .clr(in_2));
  Register #(.width(16)) register_13 (.D(DW), .en(pull_resistor_13_node), .Q(register_13_q), .clk(in_1), .clr(in_2));
  Register #(.width(16)) register_14 (.D(DW), .en(pull_resistor_14_node), .Q(register_14_q), .clk(in_1), .clr(in_2));
  Register #(.width(16)) register_15 (.D(DW), .en(pull_resistor_15_node), .Q(register_15_q), .clk(in_1), .clr(in_2));
  Register #(.width(16)) register_16 (.D(DW), .en(pull_resistor_16_node), .Q(register_16_q), .clk(in_1), .clr(in_2));
  assign A = decoder_3_out0 ? register_1_q : 16'bz;  // Controlled_Buffer controlled_buffer_1
  assign B = decoder_2_out0 ? register_1_q : 16'bz;  // Controlled_Buffer controlled_buffer_2
  assign A = decoder_3_out1 ? register_2_q : 16'bz;  // Controlled_Buffer controlled_buffer_3
  assign B = decoder_2_out1 ? register_2_q : 16'bz;  // Controlled_Buffer controlled_buffer_4
  assign A = decoder_3_out2 ? register_3_q : 16'bz;  // Controlled_Buffer controlled_buffer_5
  assign B = decoder_2_out2 ? register_3_q : 16'bz;  // Controlled_Buffer controlled_buffer_6
  assign A = decoder_3_out3 ? register_4_q : 16'bz;  // Controlled_Buffer controlled_buffer_7
  assign B = decoder_2_out3 ? register_4_q : 16'bz;  // Controlled_Buffer controlled_buffer_8
  assign A = decoder_3_out4 ? register_5_q : 16'bz;  // Controlled_Buffer controlled_buffer_9
  assign B = decoder_2_out4 ? register_5_q : 16'bz;  // Controlled_Buffer controlled_buffer_10
  assign A = decoder_3_out5 ? register_6_q : 16'bz;  // Controlled_Buffer controlled_buffer_11
  assign B = decoder_2_out5 ? register_6_q : 16'bz;  // Controlled_Buffer controlled_buffer_12
  assign A = decoder_3_out6 ? register_7_q : 16'bz;  // Controlled_Buffer controlled_buffer_13
  assign B = decoder_2_out6 ? register_7_q : 16'bz;  // Controlled_Buffer controlled_buffer_14
  assign A = decoder_3_out7 ? register_8_q : 16'bz;  // Controlled_Buffer controlled_buffer_15
  assign B = decoder_2_out7 ? register_8_q : 16'bz;  // Controlled_Buffer controlled_buffer_16
  assign A = decoder_3_out8 ? register_9_q : 16'bz;  // Controlled_Buffer controlled_buffer_17
  assign B = decoder_2_out8 ? register_9_q : 16'bz;  // Controlled_Buffer controlled_buffer_18
  assign A = decoder_3_out9 ? register_10_q : 16'bz;  // Controlled_Buffer controlled_buffer_19
  assign B = decoder_2_out9 ? register_10_q : 16'bz;  // Controlled_Buffer controlled_buffer_20
  assign A = decoder_3_out10 ? register_11_q : 16'bz;  // Controlled_Buffer controlled_buffer_21
  assign B = decoder_2_out10 ? register_11_q : 16'bz;  // Controlled_Buffer controlled_buffer_22
  assign A = decoder_3_out11 ? register_12_q : 16'bz;  // Controlled_Buffer controlled_buffer_23
  assign B = decoder_2_out11 ? register_12_q : 16'bz;  // Controlled_Buffer controlled_buffer_24
  assign A = decoder_3_out12 ? register_13_q : 16'bz;  // Controlled_Buffer controlled_buffer_25
  assign B = decoder_2_out12 ? register_13_q : 16'bz;  // Controlled_Buffer controlled_buffer_26
  assign A = decoder_3_out13 ? register_14_q : 16'bz;  // Controlled_Buffer controlled_buffer_27
  assign B = decoder_2_out13 ? register_14_q : 16'bz;  // Controlled_Buffer controlled_buffer_28
  assign A = decoder_3_out14 ? register_15_q : 16'bz;  // Controlled_Buffer controlled_buffer_29
  assign B = decoder_2_out14 ? register_15_q : 16'bz;  // Controlled_Buffer controlled_buffer_30
  assign A = decoder_3_out15 ? register_16_q : 16'bz;  // Controlled_Buffer controlled_buffer_31
  assign B = decoder_2_out15 ? register_16_q : 16'bz;  // Controlled_Buffer controlled_buffer_32
endmodule

module \Декодер  (
  input  [3:0] in_1,
  output out_2,
  output out_3,
  output out_4,
  output out_5,
  output out_6,
  output out_7,
  output out_8,
  output out_9,
  output out_10,
  output out_11,
  output out_12,
  output out_13,
  output out_14,
  output out_15,
  output out_16,
  output out_17
);

  wire and_1_out, and_2_out, and_3_out, and_4_out, and_5_out, and_6_out, and_7_out, and_8_out, not_1_out,
       not_2_out, not_3_out, not_4_out;

  not not_1 (not_1_out, in_1[0]);
  not not_2 (not_2_out, in_1[1]);
  not not_3 (not_3_out, in_1[2]);
  not not_4 (not_4_out, in_1[3]);
  and and_1 (and_1_out, not_1_out, not_2_out);
  and and_2 (and_2_out, not_3_out, not_4_out);
  and and_3 (and_3_out, not_1_out, in_1[1]);
  and and_4 (and_4_out, in_1[0], not_2_out);
  and and_5 (and_5_out, in_1[0], in_1[1]);
  and and_6 (and_6_out, in_1[2], not_4_out);
  and and_7 (and_7_out, in_1[3], not_3_out);
  and and_8 (and_8_out, in_1[3], in_1[2]);
  and and_9 (out_2, and_1_out, and_2_out);
  and and_10 (out_3, and_2_out, and_4_out);
  and and_11 (out_4, and_3_out, and_2_out);
  and and_12 (out_5, and_2_out, and_5_out);
  and and_13 (out_6, and_1_out, and_6_out);
  and and_14 (out_7, and_4_out, and_6_out);
  and and_15 (out_8, and_6_out, and_3_out);
  and and_16 (out_9, and_6_out, and_5_out);
  and and_17 (out_10, and_1_out, and_7_out);
  and and_18 (out_11, and_7_out, and_4_out);
  and and_19 (out_12, and_3_out, and_7_out);
  and and_20 (out_13, and_7_out, and_5_out);
  and and_21 (out_14, and_1_out, and_8_out);
  and and_22 (out_15, and_8_out, and_4_out);
  and and_23 (out_16, and_3_out, and_8_out);
  and and_24 (out_17, and_8_out, and_5_out);
endmodule

module \Сдвиг  (
  input  in_1,
  input  in_2,
  input  in_3,
  input  [3:0] in_4,
  output out_5,
  output out_6,
  output out_7
);

  wire decoder_1_out0, decoder_1_out1, decoder_1_out2;

  Decoder #(.select(4)) decoder_1 (
    .out0(decoder_1_out0), .out1(decoder_1_out1), .out2(decoder_1_out2), .sel(in_4));  // open: out3, out4, out5, out6, out7, out8, out9, out10, out11, out12, out13, out14, out15, en
  assign out_6 = decoder_1_out0 ? in_1 : 1'bz;  // Controlled_Buffer controlled_buffer_1
  assign out_5 = decoder_1_out0 ? in_2 : 1'bz;  // Controlled_Buffer controlled_buffer_2
  assign out_5 = decoder_1_out1 ? in_1 : 1'bz;  // Controlled_Buffer controlled_buffer_3
  assign out_7 = decoder_1_out1 ? in_2 : 1'bz;  // Controlled_Buffer controlled_buffer_4
  assign out_7 = decoder_1_out2 ? in_1 : 1'bz;  // Controlled_Buffer controlled_buffer_5
  assign out_7 = decoder_1_out0 ? in_3 : 1'bz;  // Controlled_Buffer controlled_buffer_6
  assign out_6 = decoder_1_out1 ? in_3 : 1'bz;  // Controlled_Buffer controlled_buffer_7
  assign out_5 = decoder_1_out2 ? in_3 : 1'bz;  // Controlled_Buffer controlled_buffer_8
  assign out_6 = decoder_1_out2 ? in_2 : 1'bz;  // Controlled_Buffer controlled_buffer_9
endmodule

module \АЛУ  (
  input  in_1,
  input  [3:0] in_2,
  input  [15:0] in_3,
  input  [15:0] in_4,
  input  [3:0] in_5,
  output out_6,
  output [15:0] out_7,
  output out_8
);

  wire adder_1_cout, comparator_1_eq, comparator_1_gt, comparator_1_lt, not_1_out, or_2_out, or_3_out,
       subtractor_1_bout;
  wire [15:0] adder_1_out, and_1_out, bit_extender_1_out, bit_extender_2_out, bit_extender_3_out,
       bit_extender_4_out, bit_extender_5_out, bit_extender_6_out, or_1_out, shifter_1_out, shifter_2_out,
       shifter_3_out, subtractor_1_out, xor_1_out;

  Adder #(.width(16)) adder_1 (.a(in_3), .b(in_4), .out(adder_1_out), .cin(in_1), .cout(adder_1_cout));
  Subtractor #(.width(16)) subtractor_1 (
    .a(in_3), .b(in_4), .out(subtractor_1_out), .bin(in_1), .bout(subtractor_1_bout));
  Comparator #(.width(16)) comparator_1 (
    .a(in_3), .b(in_4), .gt(comparator_1_gt), .eq(comparator_1_eq), .lt(comparator_1_lt));
  Shifter #(.width(16), .shift("lr")) shifter_1 (.in(in_3), .\dist (in_5), .out(shifter_1_out));
  Shifter #(.width(16)) shifter_2 (.in(in_3), .\dist (in_5), .out(shifter_2_out));
  Shifter #(.width(16), .shift("ar")) shifter_3 (.in(in_3), .\dist (in_5), .out(shifter_3_out));
  assign and_1_out = in_4 & in_3;  // AND_Gate and_1, 16 bits wide
  assign or_1_out = in_4 | in_3;  // OR_Gate or_1, 16 bits wide
  assign xor_1_out = in_4 ^ in_3;  // XOR_Gate xor_1, 16 bits wide
  or or_2 (or_2_out, comparator_1_gt, comparator_1_eq);
  or or_3 (or_3_out, comparator_1_eq, comparator_1_lt);
  Multiplexer multiplexer_1 (.in0(adder_1_cout), .in1(subtractor_1_bout), .out(out_6), .sel(in_2[0]), .en(1'b1));
  assign bit_extender_1_out = {{15{1'b0}}, comparator_1_eq};  // Bit_Extender bit_extender_1
  not not_1 (not_1_out, comparator_1_eq);
  assign bit_extender_2_out = {{15{1'b0}}, not_1_out};  // Bit_Extender bit_extender_2
  assign bit_extender_3_out = {{15{1'b0}}, or_2_out};  // Bit_Extender bit_extender_3
  assign bit_extender_4_out = {{15{1'b0}}, or_3_out};  // Bit_Extender bit_extender_4
  assign bit_extender_5_out = {{15{1'b0}}, comparator_1_gt};  // Bit_Extender bit_extender_5
  assign bit_extender_6_out = {{15{1'b0}}, comparator_1_lt};  // Bit_Extender bit_extender_6
  Multiplexer #(.select(4), .width(16)) multiplexer_2 (
    .in0(adder_1_out), .in1(subtractor_1_out), .in2(shifter_1_out), .in3(shifter_2_out), .in4(shifter_3_out),
    .in5(bit_extender_1_out), .in6(bit_extender_2_out), .in7(bit_extender_5_out), .in8(bit_extender_6_out),
    .in9(bit_extender_3_out), .in10(bit_extender_4_out), .in11(and_1_out), .in12(or_1_out), .out(out_7),
    .sel(in_2), .en(1'b1));  // open: in13, in14, in15
endmodule

module Control_Unit (
  input  [15:0] in_1,
  input  [15:0] in_2,
  input  in_3,
  input  in_4,
  output [1:0] MUX_B,
  output [3:0] COM_ALU,
  output BRANCH,
  output E_OP,
  output out_9,
  output out_10,
  output _1,
  output _2,
  output _3,
  output [1:0] MUX_DW,
  output EW,
  output out_16,
  output out_17,
  output MUX_A,
  output MUX_OP,
  output out_20
);

  wire and_1_out, and_2_out, comparator_1_eq, decoder_1_out0, decoder_1_out1, decoder_1_out2, decoder_1_out4,
       decoder_1_out5, decoder_1_out6, decoder_1_out7, decoder_1_out8, decoder_1_out10, decoder_1_out12,
       decoder_1_out13, not_1_out, or_7_out;
  wire [1:0] or_1_out;
  wire [3:0] multiplexer_1_out, or_3_out, register_1_q;

  Multiplexer #(.select(2), .width(4)) multiplexer_1 (
    .in0(or_3_out), .in1({in_1[3:1], 1'b0}), .in2({in_1[2:0], 1'b0}), .out(multiplexer_1_out),
    .sel(or_1_out), .en(1'b1));  // open: in3
  buf or_1 (or_1_out[0], decoder_1_out2);  // OR_Gate
  buf or_2 (or_1_out[1], decoder_1_out4);  // OR_Gate
  or or_3 (or_3_out[0], decoder_1_out6, decoder_1_out0, decoder_1_out12);
  or or_4 (or_3_out[1], decoder_1_out6, decoder_1_out1);
  or or_5 (or_3_out[2], decoder_1_out6, decoder_1_out12);
  or or_6 (or_3_out[3], decoder_1_out12, 1'b0);
  not not_1 (not_1_out, in_3);
  Decoder #(.select(4)) decoder_1 (
    .out0(decoder_1_out0), .out1(decoder_1_out1), .out2(decoder_1_out2), .out4(decoder_1_out4),
    .out5(decoder_1_out5), .out6(decoder_1_out6), .out7(decoder_1_out7), .out8(decoder_1_out8),
    .out10(decoder_1_out10), .out12(decoder_1_out12), .out13(decoder_1_out13), .sel(register_1_q), .en(1'b1));  // open: out3, out9, out11, out14, out15
  Register #(.width(4)) register_1 (.D(multiplexer_1_out), .Q(register_1_q), .clk(not_1_out), .clr(in_4));  // open: en
  or or_7 (or_7_out, decoder_1_out12, decoder_1_out10);
  Comparator #(.width(4)) comparator_1 (.a(in_1[3:0]), .b(4'b1010), .eq(comparator_1_eq));  // open: gt, lt
  or or_8 (E_OP, decoder_1_out1, decoder_1_out0, decoder_1_out8);
  buf or_9 (BRANCH, decoder_1_out10);  // OR_Gate
  and and_1 (and_1_out, comparator_1_eq, decoder_1_out2);
  buf or_10 (out_10, decoder_1_out5);  // OR_Gate
  or or_11 (out_9, decoder_1_out5, decoder_1_out6);
  buf or_12 (_2, decoder_1_out1);  // OR_Gate
  buf or_13 (_1, decoder_1_out0);  // OR_Gate
  buf or_14 (MUX_DW[1], decoder_1_out8);  // OR_Gate
  buf or_15 (_3, decoder_1_out6);  // OR_Gate
  Multiplexer #(.width(4)) multiplexer_2 (.in0(4'b0000), .in1(in_2[3:0]), .out(COM_ALU), .sel(or_7_out), .en(1'b1));
  or or_16 (EW, decoder_1_out7, decoder_1_out8, decoder_1_out13);
  buf or_17 (MUX_DW[0], decoder_1_out13);  // OR_Gate
  buf or_18 (out_16, decoder_1_out2);  // OR_Gate
  buf or_19 (out_17, decoder_1_out2);  // OR_Gate
  or or_20 (MUX_B[1], decoder_1_out6, decoder_1_out8, and_1_out);
  or or_21 (MUX_B[0], decoder_1_out0, decoder_1_out1, and_1_out);
  or or_22 (MUX_A, decoder_1_out10, decoder_1_out4, and_2_out, decoder_1_out12);
  and and_2 (and_2_out, decoder_1_out8, in_1[12]);
  buf or_23 (out_20, 1'b0);  // OR_Gate
  or or_24 (MUX_OP, decoder_1_out5, decoder_1_out6, decoder_1_out10);
endmodule

module ALU (
  input  Ci,
  input  [15:0] A,
  input  [15:0] B,
  input  [3:0] ALU_OP,
  input  [3:0] in_5,
  output [15:0] out_6,
  output [15:0] FLAGS
);

  wire adder_1_cout, and_1_out, and_3_out, and_4_out, not_2_out, not_3_out, not_4_out, or_1_out, xor_1_out;
  wire [15:0] adder_1_out, and_2_out, multiplexer_1_out, not_1_out, or_2_out, shifter_1_out, shifter_2_out,
       shifter_3_out, xor_3_out;

  or or_1 (or_1_out, Ci, ALU_OP[2]);
  and and_1 (and_1_out, or_1_out, ALU_OP[0]);
  Multiplexer #(.width(16)) multiplexer_1 (
    .in0(B), .in1(not_1_out), .out(multiplexer_1_out), .sel(ALU_OP[1]), .en(1'b1));
  assign not_1_out = ~B;  // NOT_Gate not_1, 16 bits wide
  xor xor_1 (xor_1_out, and_1_out, ALU_OP[1]);
  Adder #(.width(16)) adder_1 (.a(A), .b(multiplexer_1_out), .out(adder_1_out), .cin(xor_1_out), .cout(adder_1_cout));
  xor xor_2 (FLAGS[1], adder_1_cout, ALU_OP[1]);
  assign and_2_out = A & multiplexer_1_out;  // AND_Gate and_2, 16 bits wide
  assign or_2_out = A | multiplexer_1_out;  // OR_Gate or_2, 16 bits wide
  assign xor_3_out = A ^ multiplexer_1_out;  // XOR_Gate xor_3, 16 bits wide
  Shifter #(.width(16), .shift("lr")) shifter_1 (.in(A), .\dist (in_5), .out(shifter_1_out));
  Shifter #(.width(16)) shifter_2 (.in(A), .\dist (in_5), .out(shifter_2_out));
  Shifter #(.width(16), .shift("ar")) shifter_3 (.in(A), .\dist (in_5), .out(shifter_3_out));
  not not_2 (not_2_out, A[15]);
  not not_3 (not_3_out, B[15]);
  and and_3 (and_3_out, B[15], not_2_out, FLAGS[2]);
  or or_3 (FLAGS[3], and_3_out, and_4_out);
  not not_4 (not_4_out, FLAGS[2]);
  and and_4 (and_4_out, not_3_out, A[15], not_4_out);
  Multiplexer #(.select(4), .width(16)) multiplexer_2 (
    .in0(adder_1_out), .in1(adder_1_out), .in2(adder_1_out), .in3(adder_1_out), .in4(and_2_out),
    .in5(or_2_out), .in6(xor_3_out), .in7(adder_1_out), .in8(shifter_1_out), .in9(shifter_2_out),
    .in10(shifter_3_out), .out({FLAGS[2], out_6[14:0]}), .sel(ALU_OP), .en(1'b1));  // open: in11, in12, in13, in14, in15
  Comparator #(.width(16)) comparator_1 (.a({FLAGS[2], out_6[14:0]}), .b({16{1'b0}}), .eq(FLAGS[0]));  // open: gt, lt

  assign FLAGS[15:4] = {12{1'b0}};
  assign out_6[15] = FLAGS[2];
endmodule

module test (
  input  Z,
  input  C,
  input  S,
  input  O,
  output out_5,
  output out_6,
  output out_7,
  output out_8
);
endmodule

module FLAGS (
  input  [15:0] in_1,
  input  [15:0] in_2,
  input  CLOCK,
  input  RESET,
  output [15:0] out_5
);

  Register #(.width(1)) register_1 (.D(in_1[0]), .en(in_2[0]), .Q(out_5[0]), .clk(CLOCK), .clr(RESET));
  Register #(.width(1)) register_2 (.D(in_1[1]), .en(in_2[1]), .Q(out_5[1]), .clk(CLOCK), .clr(RESET));
  Register #(.width(1)) register_3 (.D(in_1[2]), .en(in_2[2]), .Q(out_5[2]), .clk(CLOCK), .clr(RESET));
  Register #(.width(1)) register_4 (.D(in_1[3]), .en(in_2[3]), .Q(out_5[3]), .clk(CLOCK), .clr(RESET));

  assign out_5[15:4] = {12{1'b0}};
endmodule
